// Logisim project 2bit adder.circ as structural Verilog: 1 circuit, main circuit main
module main (
  input  in_1,
  input  in_2,
  input  in_3,
  input  in_4,
  output out_5,
  output out_6,
  output out_7
);

  wire and_1_out, and_2_out, and_3_out, xor_2_out;

  xor xor_1 (out_7, in_2, in_4);
  and and_1 (and_1_out, in_2, in_4);
  xor xor_2 (xor_2_out, in_1, in_3);
  and and_2 (and_2_out, in_1, in_3);
  xor xor_3 (out_6, and_1_out, xor_2_out);
  and and_3 (and_3_out, and_1_out, xor_2_out);
  or or_1 (out_5, and_3_out, and_2_out);
endmodule
