// Logisim project 3-bit block cipher.circ as structural Verilog: 1 circuit, main circuit main
module main (
  input  x0,
  input  x1,
  input  x2,
  output y0,
  output y1,
  output y2
);

  wire xor_1_out, xor_2_out;

  xor xor_1 (xor_1_out, x2, x2);
  buf xor_2 (xor_2_out, x0);  // XOR_Gate
  xor xor_3 (y1, x1, xor_1_out);
  xor xor_4 (y0, x2, xor_2_out);
  xor xor_5 (y2, x2, x1);

  // Notes on the sheet:
  //   3-bit block cipher
endmodule
