// Logisim project Caesar shift.circ as structural Verilog: 1 circuit, main circuit main
module main (
  input  [2:0] in_1,
  input  [1:0] Encode,
  input  [2:0] in_3,
  input  [1:0] Decode,
  output [2:0] out_5,
  output [2:0] out_6
);

  Shifter #(.width(3), .shift("rl")) shifter_1 (.in(in_1), .\dist (Encode), .out(out_5));
  Shifter #(.width(3), .shift("rr")) shifter_2 (.in(in_3), .\dist (Decode), .out(out_6));

  // Notes on the sheet:
  //   Caesar Shift -- with only one component
endmodule
