// Logisim project Caesar shift3.circ as structural Verilog: 1 circuit, main circuit main
module main (
  input  [3:0] plaintext,
  input  [3:0] key,
  input  [1:0] shift,
  input  [3:0] ciphertext,
  input  [1:0] shift_2,
  input  [3:0] key_2,
  output [3:0] ciphertext_2,
  output [3:0] plaintext_2
);

  wire [3:0] shifter_1_out, xor_1_out;

  Shifter #(.width(4), .shift("rr")) shifter_1 (.in(ciphertext), .\dist (shift_2), .out(shifter_1_out));
  assign xor_1_out = plaintext ^ key;  // XOR_Gate xor_1, 4 bits wide
  Shifter #(.width(4), .shift("rl")) shifter_2 (.in(xor_1_out), .\dist (shift), .out(ciphertext_2));
  assign plaintext_2 = shifter_1_out ^ key_2;  // XOR_Gate xor_2, 4 bits wide

  // Notes on the sheet:
  //   Encode
  //   Decode
  //   Caesar Shift -- with bit transposition
endmodule
