// Logisim project Lab 2 challenge.circ as structural Verilog: 1 circuit, main circuit main
module main (
  input  x,
  input  y,
  input  A,
  input  A_2,
  input  B,
  input  A_3,
  input  B_2,
  input  in_8,
  input  in_9,
  output out_10,
  output out_11,
  output out_12,
  output out_13,
  output out_14
);

  wire and_1_out, and_2_out, nor_1_out, nor_2_out, nor_3_out, nor_4_out, nor_5_out, nor_6_out, nor_8_out,
       nor_9_out, nor_10_out, nor_11_out, nor_13_out, nor_14_out, nor_15_out, not_1_out, not_2_out;

  not not_1 (not_1_out, x);
  and and_1 (and_1_out, not_1_out, y);
  and and_2 (and_2_out, x, not_2_out);
  not not_2 (not_2_out, y);
  nor nor_1 (nor_1_out, A, B);
  nor nor_2 (nor_2_out, A, B);
  nor nor_3 (nor_3_out, A_3, A_3);
  nor nor_4 (nor_4_out, B_2, B_2);
  nor nor_5 (nor_5_out, in_8, in_8);
  nor nor_6 (nor_6_out, in_9, in_9);
  or or_1 (out_10, and_1_out, and_2_out);
  nor nor_7 (out_12, nor_1_out, nor_2_out);
  nor nor_8 (nor_8_out, A_3, B_2);
  nor nor_9 (nor_9_out, nor_3_out, nor_4_out);
  nor nor_10 (nor_10_out, nor_5_out, nor_6_out);
  nor nor_11 (nor_11_out, in_9, in_8);
  nor nor_12 (out_14, nor_10_out, nor_11_out);
  nor nor_13 (nor_13_out, nor_8_out, nor_9_out);
  nor nor_14 (nor_14_out, nor_8_out, nor_9_out);
  nor nor_15 (nor_15_out, nor_13_out, nor_14_out);
  nor nor_16 (out_11, A_2, A_2);
  nor nor_17 (out_13, nor_15_out, nor_15_out);

  // Notes on the sheet:
  //   XOR Circuit
  //   OR Circuit made with NOR gates
  //   XOR Circuit made with NOR gates
  //   Simpler XOR Circuit with NOR gates
  //   NOT Circuit made with NOR gates
endmodule
