// Logisim project Q4 Practice.circ as structural Verilog: 1 circuit, main circuit main
module main (
  input  in_1,
  input  in_2,
  output out_3
);

  wire clock_1_out, d_ff_1_q, d_ff_2_q, not_1_out, xor_1_out, xor_2_out;

  Clock clock_1 (.out(clock_1_out));
  not not_1 (not_1_out, in_2);
  xor xor_1 (xor_1_out, not_1_out, d_ff_1_q);
  D_Flip_Flop d_ff_1 (.clk(clock_1_out), .D(xor_1_out), .Q(d_ff_1_q), .reset(in_1));  // open: Qn, preset, en
  xor xor_2 (xor_2_out, in_2, d_ff_2_q);
  D_Flip_Flop d_ff_2 (.clk(clock_1_out), .D(xor_2_out), .Q(d_ff_2_q), .reset(in_1));  // open: Qn, preset, en
  nand nand_1 (out_3, d_ff_2_q, d_ff_1_q);
endmodule
