// Logisim project Y86-cpu.circ as structural Verilog
// ALU
module Do_not_click_here__double_click_module_in_circuit_ALU (
  input  [31:0] aluB,
  input  [31:0] aluA,
  input  [3:0] \function ,
  output O,
  output [31:0] valE,
  output Z,
  output S
);

  wire adder_1_cout, subtractor_1_bout;
  wire [31:0] adder_1_out, and_1_out, or_1_out, subtractor_1_out, xor_1_out;

  Adder #(.width(32)) adder_1 (.a(aluB), .b(aluA), .out(adder_1_out), .cout(adder_1_cout));  // open: cin
  Subtractor #(.width(32)) subtractor_1 (
    .a(aluB), .b(aluA), .out(subtractor_1_out), .bout(subtractor_1_bout));  // open: bin
  assign and_1_out = aluB & aluA;  // AND_Gate and_1, 32 bits wide
  assign or_1_out = aluB | aluA;  // OR_Gate or_1, 32 bits wide
  assign xor_1_out = aluB ^ aluA;  // XOR_Gate xor_1, 32 bits wide
  Multiplexer #(.select(4), .width(32), .enable("false")) multiplexer_1 (
    .in0(adder_1_out), .in1(subtractor_1_out), .in2(and_1_out), .in3(or_1_out), .in4(xor_1_out),
    .in5({32{1'b0}}), .in6({32{1'b0}}), .in7({32{1'b0}}), .in8({32{1'b0}}), .in9({32{1'b0}}),
    .in10({32{1'b0}}), .in11({32{1'b0}}), .in12({32{1'b0}}), .in13({32{1'b0}}), .in14({32{1'b0}}),
    .in15({32{1'b0}}), .out({S, valE[30:0]}), .sel(\function ));
  Multiplexer #(.select(4), .enable("false")) multiplexer_2 (
    .in0(adder_1_cout), .in1(subtractor_1_bout), .in2(1'b0), .in3(1'b0), .in4(1'b0), .in5(1'b0), .in6(1'b0),
    .in7(1'b0), .in8(1'b0), .in9(1'b0), .in10(1'b0), .in11(1'b0), .in12(1'b0), .in13(1'b0), .in14(1'b0),
    .in15(1'b0), .out(O), .sel(\function ));
  nor nor_1 (Z, valE[0], valE[1], valE[2], valE[3], valE[4], valE[5], valE[6], valE[7], valE[8], valE[9], valE[10], valE[11], valE[12], valE[13], valE[14], valE[15], valE[17], valE[18], valE[19], valE[20], valE[21], valE[22], valE[23], valE[24], valE[25], valE[26], valE[27], valE[28], valE[29], valE[30], S, valE[16]);

  assign valE[31] = S;

  // Notes on the sheet:
  //   Note: our CPU only implements 5 functions
  //   currently (+, - ^, v, xor), although with 4
  //   bits we could have up to 16 functions. The
  //   C (carry) bit is only set for + and -.
  //   The wire splitter and NOR gate look very
  //   impressive, but do nothing more exciting
  //   than setting Z to True if all the bits of the
  //   result are 0 (that is, if result = 0).
  //   (Previously labeled C for carry
  //   rather than O for overflow)
endmodule

module main___START_HERE (
  output bch
);

  wire Clock_out, d_ff_1_q,
       do_not_click_here_double_click_module_in_circuit_main_memory_1_illegal_memory_access,
       do_not_click_here_double_click_module_in_circuit_memory_1_write, not_1_out, Reset_out;
  wire [3:0] do_not_click_here_double_click_module_in_circuit_decode_1_dste,
       do_not_click_here_double_click_module_in_circuit_decode_1_dstm,
       do_not_click_here_double_click_module_in_circuit_decode_1_srca,
       do_not_click_here_double_click_module_in_circuit_decode_1_srcb,
       do_not_click_here_double_click_module_in_circuit_fetch_parse_instr_1_icd,
       do_not_click_here_double_click_module_in_circuit_fetch_parse_instr_1_ifn,
       do_not_click_here_double_click_module_in_circuit_fetch_parse_instr_1_ra,
       do_not_click_here_double_click_module_in_circuit_fetch_parse_instr_1_rb, multiplexer_1_out;
  wire [15:0] do_not_click_here_double_click_module_in_circuit_main_memory_1_second_word;
  wire [31:0] do_not_click_here_double_click_module_in_circuit_execute_1_vale,
       do_not_click_here_double_click_module_in_circuit_fetch_parse_instr_1_valc,
       do_not_click_here_double_click_module_in_circuit_fetch_parse_instr_1_valp,
       do_not_click_here_double_click_module_in_circuit_main_memory_1_first_word,
       do_not_click_here_double_click_module_in_circuit_memory_1_address,
       do_not_click_here_double_click_module_in_circuit_memory_1_data,
       do_not_click_here_double_click_module_in_circuit_nextpc_1_nextpc,
       do_not_click_here_double_click_module_in_circuit_registers_1_eax,
       do_not_click_here_double_click_module_in_circuit_registers_1_ebp,
       do_not_click_here_double_click_module_in_circuit_registers_1_ebx,
       do_not_click_here_double_click_module_in_circuit_registers_1_ecx,
       do_not_click_here_double_click_module_in_circuit_registers_1_edi,
       do_not_click_here_double_click_module_in_circuit_registers_1_edx,
       do_not_click_here_double_click_module_in_circuit_registers_1_esi,
       do_not_click_here_double_click_module_in_circuit_registers_1_esp,
       do_not_click_here_double_click_module_in_circuit_registers_1_vala,
       do_not_click_here_double_click_module_in_circuit_registers_1_valb, Program_Counter_q;

  Button Reset (.out(Reset_out));
  Clock Clock (.out(Clock_out));
  LED led_1 (.in(do_not_click_here_double_click_module_in_circuit_main_memory_1_illegal_memory_access));
  Do_not_click_here__double_click_module_in_circuit_Main_Memory do_not_click_here_double_click_module_in_circuit_main_memory_1 (
    .Data_from_Memory_Stage(do_not_click_here_double_click_module_in_circuit_memory_1_data),
    .Write(do_not_click_here_double_click_module_in_circuit_memory_1_write), .Clock(Clock_out),
    .First_Word(do_not_click_here_double_click_module_in_circuit_main_memory_1_first_word),
    .Second_Word(do_not_click_here_double_click_module_in_circuit_main_memory_1_second_word),
    .Illegal_Memory_Access(do_not_click_here_double_click_module_in_circuit_main_memory_1_illegal_memory_access),
    .Addr_from_Memory_Stage(do_not_click_here_double_click_module_in_circuit_memory_1_address),
    .Program_Counter(Program_Counter_q), .Substep_Number(d_ff_1_q));
  D_Flip_Flop d_ff_1 (
    .clk(Clock_out), .D(not_1_out), .Q(d_ff_1_q), .preset(1'b0), .en(1'b1), .reset(Reset_out));  // open: Qn
  not not_1 (not_1_out, d_ff_1_q);
  Register #(.width(32)) Program_Counter (
    .D(do_not_click_here_double_click_module_in_circuit_nextpc_1_nextpc), .en(d_ff_1_q),
    .Q(Program_Counter_q), .clk(Clock_out), .clr(Reset_out));
  highlighter__not_a_real_module highlighter_not_a_real_module_1 ();
  // Probe on do_not_click_here_double_click_module_in_circuit_fetch_parse_instr_1_icd
  // Probe on do_not_click_here_double_click_module_in_circuit_fetch_parse_instr_1_ifn
  Do_not_click_here__double_click_module_in_circuit_nextPC do_not_click_here_double_click_module_in_circuit_nextpc_1 (
    .valP(do_not_click_here_double_click_module_in_circuit_fetch_parse_instr_1_valp),
    .valC(do_not_click_here_double_click_module_in_circuit_fetch_parse_instr_1_valc),
    .valM(do_not_click_here_double_click_module_in_circuit_main_memory_1_first_word),
    .nextPC(do_not_click_here_double_click_module_in_circuit_nextpc_1_nextpc), .bch(bch),
    .iCd(do_not_click_here_double_click_module_in_circuit_fetch_parse_instr_1_icd));
  Do_not_click_here__double_click_module_in_circuit_Memory do_not_click_here_double_click_module_in_circuit_memory_1 (
    .valE(do_not_click_here_double_click_module_in_circuit_execute_1_vale),
    .valA(do_not_click_here_double_click_module_in_circuit_registers_1_vala),
    .valP(do_not_click_here_double_click_module_in_circuit_fetch_parse_instr_1_valp),
    .Address(do_not_click_here_double_click_module_in_circuit_memory_1_address),
    .Data(do_not_click_here_double_click_module_in_circuit_memory_1_data),
    .Write(do_not_click_here_double_click_module_in_circuit_memory_1_write),
    .iCd(do_not_click_here_double_click_module_in_circuit_fetch_parse_instr_1_icd));
  Do_not_click_here__double_click_module_in_circuit_Execute do_not_click_here_double_click_module_in_circuit_execute_1 (
    .valA(do_not_click_here_double_click_module_in_circuit_registers_1_vala),
    .valC(do_not_click_here_double_click_module_in_circuit_fetch_parse_instr_1_valc),
    .valB(do_not_click_here_double_click_module_in_circuit_registers_1_valb), .Step(d_ff_1_q), .Bch(bch),
    .iCd(do_not_click_here_double_click_module_in_circuit_fetch_parse_instr_1_icd),
    .iFn(do_not_click_here_double_click_module_in_circuit_fetch_parse_instr_1_ifn),
    .valE(do_not_click_here_double_click_module_in_circuit_execute_1_vale), .Clock(Clock_out),
    .Reset(Reset_out));
  Do_not_click_here__double_click_module_in_circuit_Decode do_not_click_here_double_click_module_in_circuit_decode_1 (
    .rA(do_not_click_here_double_click_module_in_circuit_fetch_parse_instr_1_ra),
    .rB(do_not_click_here_double_click_module_in_circuit_fetch_parse_instr_1_rb),
    .srcA(do_not_click_here_double_click_module_in_circuit_decode_1_srca),
    .srcB(do_not_click_here_double_click_module_in_circuit_decode_1_srcb),
    .dstE(do_not_click_here_double_click_module_in_circuit_decode_1_dste),
    .dstM(do_not_click_here_double_click_module_in_circuit_decode_1_dstm),
    .iCd(do_not_click_here_double_click_module_in_circuit_fetch_parse_instr_1_icd));
  Do_not_click_here__double_click_module_in_circuit_Fetch___Parse_Instr do_not_click_here_double_click_module_in_circuit_fetch_parse_instr_1 (
    .Bits_0_to_31(do_not_click_here_double_click_module_in_circuit_main_memory_1_first_word),
    .Bits_32_to_47(do_not_click_here_double_click_module_in_circuit_main_memory_1_second_word),
    .iCd(do_not_click_here_double_click_module_in_circuit_fetch_parse_instr_1_icd),
    .IFn(do_not_click_here_double_click_module_in_circuit_fetch_parse_instr_1_ifn),
    .rA(do_not_click_here_double_click_module_in_circuit_fetch_parse_instr_1_ra),
    .rB(do_not_click_here_double_click_module_in_circuit_fetch_parse_instr_1_rb),
    .valC(do_not_click_here_double_click_module_in_circuit_fetch_parse_instr_1_valc),
    .valP(do_not_click_here_double_click_module_in_circuit_fetch_parse_instr_1_valp), .Substep(d_ff_1_q),
    .Clock(Clock_out), .Program_Counter(Program_Counter_q));
  // Probe on do_not_click_here_double_click_module_in_circuit_fetch_parse_instr_1_rb
  // Probe on do_not_click_here_double_click_module_in_circuit_fetch_parse_instr_1_ra
  Do_not_click_here__double_click_module_in_circuit_Registers do_not_click_here_double_click_module_in_circuit_registers_1 (
    .dstE(multiplexer_1_out), .dstM(do_not_click_here_double_click_module_in_circuit_decode_1_dstm),
    .valA(do_not_click_here_double_click_module_in_circuit_registers_1_vala),
    .valB(do_not_click_here_double_click_module_in_circuit_registers_1_valb),
    .valE(do_not_click_here_double_click_module_in_circuit_execute_1_vale),
    .valM(do_not_click_here_double_click_module_in_circuit_main_memory_1_first_word), .Clock(Clock_out),
    .Reset(Reset_out), .srcA(do_not_click_here_double_click_module_in_circuit_decode_1_srca),
    .srcB(do_not_click_here_double_click_module_in_circuit_decode_1_srcb),
    .eax(do_not_click_here_double_click_module_in_circuit_registers_1_eax),
    .ecx(do_not_click_here_double_click_module_in_circuit_registers_1_ecx),
    .edx(do_not_click_here_double_click_module_in_circuit_registers_1_edx),
    .ebx(do_not_click_here_double_click_module_in_circuit_registers_1_ebx),
    .esp(do_not_click_here_double_click_module_in_circuit_registers_1_esp),
    .ebp(do_not_click_here_double_click_module_in_circuit_registers_1_ebp),
    .esi(do_not_click_here_double_click_module_in_circuit_registers_1_esi),
    .edi(do_not_click_here_double_click_module_in_circuit_registers_1_edi), .Substep(d_ff_1_q));
  // Probe on do_not_click_here_double_click_module_in_circuit_decode_1_srca
  // Probe on do_not_click_here_double_click_module_in_circuit_decode_1_srcb
  Multiplexer #(.width(4), .enable("false")) multiplexer_1 (
    .in0(4'b1111), .in1(do_not_click_here_double_click_module_in_circuit_decode_1_dste),
    .out(multiplexer_1_out), .sel(bch));
  // Probe on do_not_click_here_double_click_module_in_circuit_registers_1_valb
  // Probe on do_not_click_here_double_click_module_in_circuit_registers_1_vala
  // Probe on do_not_click_here_double_click_module_in_circuit_execute_1_vale
  // Probe on do_not_click_here_double_click_module_in_circuit_registers_1_eax
  // Probe on do_not_click_here_double_click_module_in_circuit_registers_1_ecx
  // Probe on do_not_click_here_double_click_module_in_circuit_registers_1_edx
  // Probe on do_not_click_here_double_click_module_in_circuit_registers_1_ebx
  // Probe on do_not_click_here_double_click_module_in_circuit_registers_1_esp
  // Probe on do_not_click_here_double_click_module_in_circuit_registers_1_ebp
  // Probe on do_not_click_here_double_click_module_in_circuit_registers_1_esi
  // Probe on do_not_click_here_double_click_module_in_circuit_registers_1_edi
  // Probe on do_not_click_here_double_click_module_in_circuit_fetch_parse_instr_1_valc
  // Probe on do_not_click_here_double_click_module_in_circuit_fetch_parse_instr_1_valp
  // Probe on Program_Counter_q

  // Notes on the sheet:
  //   To get inside a module:
  //   (1) Make sure you're in "poke" mode, the finger button in the upper-left.
  //   (2) Click the module you want to open.
  //   (3) Double-click the magnifying glass that appears.
endmodule

// Registers
module Do_not_click_here__double_click_module_in_circuit_Registers (
  input  [3:0] dstE,
  input  [3:0] dstM,
  input  [31:0] valE,
  input  [31:0] valM,
  input  [3:0] srcA,
  input  [3:0] srcB,
  input  Clock,
  input  Reset,
  input  Substep,
  output [31:0] eax,
  output [31:0] ecx,
  output [31:0] edx,
  output [31:0] ebx,
  output [31:0] esp,
  output [31:0] ebp,
  output [31:0] esi,
  output [31:0] edi,
  output [31:0] valA,
  output [31:0] valB
);

  wire and_1_out, and_2_out, and_3_out, and_4_out, and_5_out, and_6_out, and_7_out, and_8_out,
       decoder_1_out0, decoder_1_out1, decoder_1_out2, decoder_1_out3, decoder_1_out4, decoder_1_out5,
       decoder_1_out6, decoder_1_out7, decoder_2_out0, decoder_2_out1, decoder_2_out2, decoder_2_out3,
       decoder_2_out4, decoder_2_out5, decoder_2_out6, decoder_2_out7, or_1_out, or_2_out, or_3_out,
       or_4_out, or_5_out, or_6_out, or_7_out, or_8_out;
  wire [31:0] multiplexer_1_out, multiplexer_2_out, multiplexer_3_out, multiplexer_4_out, multiplexer_5_out,
       multiplexer_6_out, multiplexer_7_out, multiplexer_8_out;

  Multiplexer #(.width(32), .enable("false")) multiplexer_1 (
    .in0(valM), .in1(valE), .out(multiplexer_1_out), .sel(decoder_1_out0));
  Multiplexer #(.width(32), .enable("false")) multiplexer_2 (
    .in0(valM), .in1(valE), .out(multiplexer_2_out), .sel(decoder_1_out1));
  Multiplexer #(.width(32), .enable("false")) multiplexer_3 (
    .in0(valM), .in1(valE), .out(multiplexer_3_out), .sel(decoder_1_out2));
  Multiplexer #(.width(32), .enable("false")) multiplexer_4 (
    .in0(valM), .in1(valE), .out(multiplexer_4_out), .sel(decoder_1_out3));
  Multiplexer #(.width(32), .enable("false")) multiplexer_5 (
    .in0(valM), .in1(valE), .out(multiplexer_5_out), .sel(decoder_1_out4));
  Multiplexer #(.width(32), .enable("false")) multiplexer_6 (
    .in0(valM), .in1(valE), .out(multiplexer_6_out), .sel(decoder_1_out5));
  Multiplexer #(.width(32), .enable("false")) multiplexer_7 (
    .in0(valM), .in1(valE), .out(multiplexer_7_out), .sel(decoder_1_out6));
  Multiplexer #(.width(32), .enable("false")) multiplexer_8 (
    .in0(valM), .in1(valE), .out(multiplexer_8_out), .sel(decoder_1_out7));
  Decoder #(.select(4), .enable("false")) decoder_1 (
    .out0(decoder_1_out0), .out1(decoder_1_out1), .out2(decoder_1_out2), .out3(decoder_1_out3),
    .out4(decoder_1_out4), .out5(decoder_1_out5), .out6(decoder_1_out6), .out7(decoder_1_out7), .sel(dstE));  // open: out8, out9, out10, out11, out12, out13, out14, out15
  Decoder #(.select(4), .enable("false")) decoder_2 (
    .out0(decoder_2_out0), .out1(decoder_2_out1), .out2(decoder_2_out2), .out3(decoder_2_out3),
    .out4(decoder_2_out4), .out5(decoder_2_out5), .out6(decoder_2_out6), .out7(decoder_2_out7), .sel(dstM));  // open: out8, out9, out10, out11, out12, out13, out14, out15
  or or_1 (or_1_out, decoder_1_out0, decoder_2_out0);
  or or_2 (or_2_out, decoder_1_out1, decoder_2_out1);
  or or_3 (or_3_out, decoder_1_out2, decoder_2_out2);
  or or_4 (or_4_out, decoder_1_out3, decoder_2_out3);
  or or_5 (or_5_out, decoder_1_out4, decoder_2_out4);
  or or_6 (or_6_out, decoder_1_out5, decoder_2_out5);
  or or_7 (or_7_out, decoder_1_out6, decoder_2_out6);
  or or_8 (or_8_out, decoder_1_out7, decoder_2_out7);
  and and_1 (and_1_out, or_1_out, Substep);
  and and_2 (and_2_out, or_2_out, Substep);
  and and_3 (and_3_out, or_3_out, Substep);
  and and_4 (and_4_out, or_4_out, Substep);
  and and_5 (and_5_out, or_5_out, Substep);
  and and_6 (and_6_out, or_6_out, Substep);
  and and_7 (and_7_out, or_7_out, Substep);
  and and_8 (and_8_out, or_8_out, Substep);
  Register #(.width(32)) u_eax (.D(multiplexer_1_out), .en(and_1_out), .Q(eax), .clk(Clock), .clr(Reset));
  Register #(.width(32)) u_ecx (.D(multiplexer_2_out), .en(and_2_out), .Q(ecx), .clk(Clock), .clr(Reset));
  Register #(.width(32)) u_edx (.D(multiplexer_3_out), .en(and_3_out), .Q(edx), .clk(Clock), .clr(Reset));
  Register #(.width(32)) u_ebx (.D(multiplexer_4_out), .en(and_4_out), .Q(ebx), .clk(Clock), .clr(Reset));
  Register #(.width(32)) u_esp (.D(multiplexer_5_out), .en(and_5_out), .Q(esp), .clk(Clock), .clr(Reset));
  Register #(.width(32)) u_ebp (.D(multiplexer_6_out), .en(and_6_out), .Q(ebp), .clk(Clock), .clr(Reset));
  Register #(.width(32)) u_esi (.D(multiplexer_7_out), .en(and_7_out), .Q(esi), .clk(Clock), .clr(Reset));
  Register #(.width(32)) u_edi (.D(multiplexer_8_out), .en(and_8_out), .Q(edi), .clk(Clock), .clr(Reset));
  Multiplexer #(.select(4), .width(32), .enable("false")) multiplexer_9 (
    .in0(eax), .in1(ecx), .in2(edx), .in3(ebx), .in4(esp), .in5(ebp), .in6(esi), .in7(edi), .in8({32{1'b0}}),
    .in9({32{1'b0}}), .in10({32{1'b0}}), .in11({32{1'b0}}), .in12({32{1'b0}}), .in13({32{1'b0}}),
    .in14({32{1'b0}}), .in15({32{1'b0}}), .out(valA), .sel(srcA));
  Multiplexer #(.select(4), .width(32), .enable("false")) multiplexer_10 (
    .in0(eax), .in1(ecx), .in2(edx), .in3(ebx), .in4(esp), .in5(ebp), .in6(esi), .in7(edi), .in8({32{1'b0}}),
    .in9({32{1'b0}}), .in10({32{1'b0}}), .in11({32{1'b0}}), .in12({32{1'b0}}), .in13({32{1'b0}}),
    .in14({32{1'b0}}), .in15({32{1'b0}}), .out(valB), .sel(srcB));
endmodule

// 16MB RAM
module Do_not_click_here__double_click_module_in_circuit_Main_Memory (
  input  [31:0] Data_from_Memory_Stage,
  input  [31:0] Addr_from_Memory_Stage,
  input  [31:0] Program_Counter,
  input  Clock,
  input  Write,
  input  Substep_Number,
  output [31:0] First_Word,
  output [15:0] Second_Word,
  output Illegal_Memory_Access
);

  wire and_1_out, not_1_out;
  wire [2:0] simple_ram_1_p5;
  wire [31:0] multiplexer_1_out;

  Multiplexer #(.width(32), .enable("false")) multiplexer_1 (
    .in0(Program_Counter), .in1(Addr_from_Memory_Stage), .out(multiplexer_1_out), .sel(Substep_Number));
  Illegal_Memory_Access illegal_memory_access_1 (
    .Substep(Substep_Number), .Address(multiplexer_1_out), .Output(Illegal_Memory_Access));
  not not_1 (not_1_out, and_1_out);
  and and_1 (and_1_out, Write, Substep_Number);
  // Simple_RAM simple_ram_1: pin names not known; wires that end beside it: multiplexer_1_out[23:0], 1'b1, Clock, not_1_out, simple_ram_1_p5, First_Word[31:24], First_Word[23:16], First_Word[15:8], First_Word[7:0], Second_Word[15:8], Second_Word[7:0]
  Multiplexer #(.width(3), .enable("false")) multiplexer_2 (
    .in0(3'b110), .in1(3'b100), .out(simple_ram_1_p5), .sel(Substep_Number));
  assign First_Word = and_1_out ? Data_from_Memory_Stage : 32'bz;  // Controlled_Buffer controlled_buffer_1
endmodule

// Fetch
module Do_not_click_here__double_click_module_in_circuit_Fetch___Parse_Instr (
  input  [31:0] Bits_0_to_31,
  input  [15:0] Bits_32_to_47,
  input  Substep,
  input  [31:0] Program_Counter,
  input  Clock,
  output [3:0] iCd,
  output [3:0] IFn,
  output [31:0] valP,
  output [3:0] rA,
  output [3:0] rB,
  output [31:0] valC
);

  wire not_1_out;
  wire [7:0] multiplexer_1_out;
  wire [31:0] adder_1_out, multiplexer_2_out, multiplexer_3_out;

  Multiplexer #(.select(4), .width(8), .enable("false")) multiplexer_1 (
    .in0({8{1'b1}}), .in1({8{1'b1}}), .in2(Bits_0_to_31[23:16]), .in3(Bits_0_to_31[23:16]),
    .in4(Bits_0_to_31[23:16]), .in5(Bits_0_to_31[23:16]), .in6(Bits_0_to_31[23:16]), .in7({8{1'b1}}),
    .in8({8{1'b1}}), .in9({8{1'b1}}), .in10(Bits_0_to_31[23:16]), .in11(Bits_0_to_31[23:16]),
    .out(multiplexer_1_out), .sel(Bits_0_to_31[31:28]));  // open: in12, in13, in14, in15
  Multiplexer #(.select(4), .width(32), .enable("false")) multiplexer_2 (
    .in0({32{1'b0}}), .in1({32{1'b0}}), .in2({32{1'b0}}), .in3({Bits_0_to_31[15:0], Bits_32_to_47}),
    .in4({Bits_0_to_31[15:0], Bits_32_to_47}), .in5({Bits_0_to_31[15:0], Bits_32_to_47}), .in6({32{1'b0}}),
    .in7({Bits_0_to_31[23:0], Bits_32_to_47[15:8]}), .in8({Bits_0_to_31[23:0], Bits_32_to_47[15:8]}),
    .in9({32{1'b0}}), .in10({32{1'b0}}), .in11({32{1'b0}}), .out(multiplexer_2_out), .sel(Bits_0_to_31[31:28]));  // open: in12, in13, in14, in15
  not not_1 (not_1_out, Substep);
  Register #(.width(4)) u_iCd (.D(Bits_0_to_31[31:28]), .en(not_1_out), .Q(iCd), .clk(Clock));  // open: clr
  Register #(.width(4)) u_iFn (.D(Bits_0_to_31[27:24]), .en(not_1_out), .Q(IFn), .clk(Clock));  // open: clr
  Register #(.width(4)) u_rA (.D(multiplexer_1_out[7:4]), .en(not_1_out), .Q(rA), .clk(Clock));  // open: clr
  Register #(.width(4)) u_rB (.D(multiplexer_1_out[3:0]), .en(not_1_out), .Q(rB), .clk(Clock));  // open: clr
  Register #(.width(32)) u_valC (.D(multiplexer_2_out), .en(not_1_out), .Q(valC), .clk(Clock));  // open: clr
  Multiplexer #(.select(4), .width(32), .enable("false")) multiplexer_3 (
    .in0({32{1'b0}}), .in1(32'h1), .in2(32'h2), .in3(32'h6), .in4(32'h6), .in5(32'h6), .in6(32'h2),
    .in7(32'h5), .in8(32'h5), .in9(32'h1), .in10(32'h2), .in11(32'h2), .in12({32{1'b0}}), .in13({32{1'b0}}),
    .in14({32{1'b0}}), .in15({32{1'b0}}), .out(multiplexer_3_out), .sel(Bits_0_to_31[31:28]));
  Adder #(.width(32)) adder_1 (
    .a(multiplexer_3_out), .b(Program_Counter), .out(adder_1_out), .cin(1'b0));  // open: cout
  Register #(.width(32)) u_valP (.D(adder_1_out), .en(not_1_out), .Q(valP), .clk(Clock));  // open: clr

  // Notes on the sheet:
  //   Which instruction would want a 0 here?
endmodule

// Decode
module Do_not_click_here__double_click_module_in_circuit_Decode (
  input  [3:0] rA,
  input  [3:0] rB,
  input  [3:0] iCd,
  output [3:0] srcA,
  output [3:0] srcB,
  output [3:0] dstE,
  output [3:0] dstM
);

  Multiplexer #(.select(4), .width(4), .enable("false")) multiplexer_1 (
    .in0(4'b1111), .in1(4'b1111), .in2(rA), .in3(4'b1111), .in4(rA), .in5(4'b1111), .in6(rA), .in7(4'b1111),
    .in8(rA), .in9(4'b0100), .in10(rA), .in11(4'b0100), .in12(4'b1111), .in13(4'b1111), .in14(4'b1111),
    .in15(4'b1111), .out(srcA), .sel(iCd));
  Multiplexer #(.select(4), .width(4), .enable("false")) multiplexer_2 (
    .in0(4'b1111), .in1(4'b1111), .in2(rB), .in3(4'b1111), .in4(rB), .in5(rB), .in6(rB), .in7(rB),
    .in8(4'b0100), .in9(4'b0100), .in10(4'b0100), .in11(4'b0100), .in12(4'b1111), .in13(4'b1111),
    .in14(4'b1111), .in15(4'b1111), .out(srcB), .sel(iCd));
  Multiplexer #(.select(4), .width(4), .enable("false")) multiplexer_3 (
    .in0(4'b1111), .in1(4'b1111), .in2(rB), .in3(rB), .in4(4'b1111), .in5(4'b1111), .in6(rB), .in7(4'b1111),
    .in8(4'b0100), .in9(4'b0100), .in10(4'b0100), .in11(4'b0100), .in12(4'b1111), .in13(4'b1111),
    .in14(4'b1111), .in15(4'b1111), .out(dstE), .sel(iCd));
  Multiplexer #(.select(4), .width(4), .enable("false")) multiplexer_4 (
    .in0(4'b1111), .in1(4'b1111), .in2(4'b1111), .in3(4'b1111), .in4(4'b1111), .in5(rA), .in6(4'b1111),
    .in7(4'b1111), .in8(4'b1111), .in9(4'b1111), .in10(4'b1111), .in11(rA), .in12(4'b1111), .in13(4'b1111),
    .in14(4'b1111), .in15(4'b1111), .out(dstM), .sel(iCd));
endmodule

// Execute
module Do_not_click_here__double_click_module_in_circuit_Execute (
  input  [31:0] valA,
  input  [31:0] valC,
  input  [31:0] valB,
  input  Clock,
  input  Reset,
  input  [3:0] iCd,
  input  [3:0] iFn,
  input  Step,
  output [31:0] valE,
  output Bch
);

  wire and_1_out, do_not_click_here_double_click_module_in_circuit_alu_1_o,
       do_not_click_here_double_click_module_in_circuit_alu_1_s,
       do_not_click_here_double_click_module_in_circuit_alu_1_z,
       do_not_click_here_double_click_module_in_circuit_equals_1_output, O_q, S_q, Z_q;
  wire [3:0] multiplexer_3_out;
  wire [31:0] multiplexer_1_out, multiplexer_2_out;

  Do_not_click_here__double_click_module_in_circuit_ALU do_not_click_here_double_click_module_in_circuit_alu_1 (
    .aluA(multiplexer_1_out), .aluB(multiplexer_2_out), .\function (multiplexer_3_out),
    .O(do_not_click_here_double_click_module_in_circuit_alu_1_o), .valE(valE),
    .Z(do_not_click_here_double_click_module_in_circuit_alu_1_z),
    .S(do_not_click_here_double_click_module_in_circuit_alu_1_s));
  Multiplexer #(.select(4), .width(32), .enable("false")) multiplexer_1 (
    .in0({32{1'b0}}), .in1({32{1'b0}}), .in2(valA), .in3(valC), .in4(valC), .in5(valC), .in6(valA),
    .in7(valC), .in8(32'hfffffffc), .in9(32'h4), .in10(32'hfffffffc), .in11(32'h4), .in12({32{1'b0}}),
    .in13({32{1'b0}}), .in14({32{1'b0}}), .in15({32{1'b0}}), .out(multiplexer_1_out), .sel(iCd));
  Multiplexer #(.select(4), .width(32), .enable("false")) multiplexer_2 (
    .in0({32{1'b0}}), .in1({32{1'b0}}), .in2({32{1'b0}}), .in3({32{1'b0}}), .in4(valB), .in5(valB),
    .in6(valB), .in7({32{1'b0}}), .in8(valB), .in9(valB), .in10(valB), .in11(valB), .in12({32{1'b0}}),
    .in13({32{1'b0}}), .in14({32{1'b0}}), .in15({32{1'b0}}), .out(multiplexer_2_out), .sel(iCd));
  Multiplexer #(.select(4), .width(4), .enable("false")) multiplexer_3 (
    .in0(4'b0000), .in1(4'b0000), .in2(4'b0000), .in3(4'b0000), .in4(4'b0000), .in5(4'b0000), .in6(iFn),
    .in7(4'b0000), .in8(4'b0000), .in9(4'b0000), .in10(4'b0000), .in11(4'b0000), .in12(4'b0000),
    .in13(4'b0000), .in14(4'b0000), .in15(4'b0000), .out(multiplexer_3_out), .sel(iCd));
  Do_not_click_here__double_click_module_in_circuit_Equals do_not_click_here_double_click_module_in_circuit_equals_1 (
    .Input_1(4'b0110), .Input_2(iCd),
    .Output(do_not_click_here_double_click_module_in_circuit_equals_1_output));
  and and_1 (and_1_out, do_not_click_here_double_click_module_in_circuit_equals_1_output, Step);
  D_Flip_Flop O (
    .clk(Clock), .D(do_not_click_here_double_click_module_in_circuit_alu_1_o), .Q(O_q), .preset(1'b0),
    .en(and_1_out), .reset(Reset));  // open: Qn
  D_Flip_Flop Z (
    .clk(Clock), .D(do_not_click_here_double_click_module_in_circuit_alu_1_z), .Q(Z_q), .preset(1'b0),
    .en(and_1_out), .reset(Reset));  // open: Qn
  D_Flip_Flop S (
    .clk(Clock), .D(do_not_click_here_double_click_module_in_circuit_alu_1_s), .Q(S_q), .preset(1'b0),
    .en(and_1_out), .reset(Reset));  // open: Qn
  Do_not_click_here__double_click_module_in_circuit_Decide_branch do_not_click_here_double_click_module_in_circuit_decide_branch_1 (
    .iCd(iCd), .Z(Z_q), .S(S_q), .O(O_q), .iFn(iFn), .Bch(Bch));
endmodule

// =
module Do_not_click_here__double_click_module_in_circuit_Equals (
  input  [3:0] Input_1,
  input  [3:0] Input_2,
  output Output
);

  wire [3:0] xnor_1_out;

  assign xnor_1_out = ~(Input_1 ^ Input_2);  // XNOR_Gate xnor_1, 4 bits wide
  and and_1 (Output, xnor_1_out[0], xnor_1_out[1], xnor_1_out[2], xnor_1_out[3]);
endmodule

// Branch?
module Do_not_click_here__double_click_module_in_circuit_Decide_branch (
  input  [3:0] iCd,
  input  Z,
  input  S,
  input  O,
  input  [3:0] iFn,
  output Bch
);

  wire do_not_click_here_double_click_module_in_circuit_equals_1_output,
       do_not_click_here_double_click_module_in_circuit_equals_2_output, multiplexer_1_out, nor_1_out,
       not_1_out, not_2_out, not_3_out, or_1_out, xor_1_out;

  Do_not_click_here__double_click_module_in_circuit_Equals do_not_click_here_double_click_module_in_circuit_equals_1 (
    .Input_1(4'b0111), .Input_2(iCd),
    .Output(do_not_click_here_double_click_module_in_circuit_equals_1_output));
  Do_not_click_here__double_click_module_in_circuit_Equals do_not_click_here_double_click_module_in_circuit_equals_2 (
    .Input_1(4'b0010), .Input_2(iCd),
    .Output(do_not_click_here_double_click_module_in_circuit_equals_2_output));
  xor xor_1 (xor_1_out, S, O);
  nor nor_1 (nor_1_out, do_not_click_here_double_click_module_in_circuit_equals_1_output, do_not_click_here_double_click_module_in_circuit_equals_2_output);
  or or_1 (or_1_out, Z, xor_1_out);
  not not_1 (not_1_out, Z);
  not not_2 (not_2_out, xor_1_out);
  not not_3 (not_3_out, or_1_out);
  Multiplexer #(.select(4), .enable("false")) multiplexer_1 (
    .in0(1'b1), .in1(or_1_out), .in2(xor_1_out), .in3(Z), .in4(not_1_out), .in5(not_2_out), .in6(not_3_out),
    .in7(1'b1), .in8(1'b1), .in9(1'b1), .in10(1'b1), .in11(1'b1), .in12(1'b1), .in13(1'b1), .in14(1'b1),
    .in15(1'b1), .out(multiplexer_1_out), .sel(iFn));
  or or_2 (Bch, nor_1_out, multiplexer_1_out);
endmodule

// Memory
module Do_not_click_here__double_click_module_in_circuit_Memory (
  input  [31:0] valE,
  input  [31:0] valA,
  input  [31:0] valP,
  input  [3:0] iCd,
  output [31:0] Address,
  output [31:0] Data,
  output Write
);

  wire do_not_click_here_double_click_module_in_circuit_equals_1_output,
       do_not_click_here_double_click_module_in_circuit_equals_2_output,
       do_not_click_here_double_click_module_in_circuit_equals_3_output;

  Do_not_click_here__double_click_module_in_circuit_Equals do_not_click_here_double_click_module_in_circuit_equals_1 (
    .Input_1(4'b0100), .Input_2(iCd),
    .Output(do_not_click_here_double_click_module_in_circuit_equals_1_output));
  Do_not_click_here__double_click_module_in_circuit_Equals do_not_click_here_double_click_module_in_circuit_equals_2 (
    .Input_1(4'b1000), .Input_2(iCd),
    .Output(do_not_click_here_double_click_module_in_circuit_equals_2_output));
  Do_not_click_here__double_click_module_in_circuit_Equals do_not_click_here_double_click_module_in_circuit_equals_3 (
    .Input_1(4'b1010), .Input_2(iCd),
    .Output(do_not_click_here_double_click_module_in_circuit_equals_3_output));
  Multiplexer #(.select(4), .width(32), .enable("false")) multiplexer_1 (
    .in0({32{1'b0}}), .in1({32{1'b0}}), .in2({32{1'b0}}), .in3({32{1'b0}}), .in4(valE), .in5(valE),
    .in6({32{1'b0}}), .in7({32{1'b0}}), .in8(valE), .in9(valA), .in10(valE), .in11(valA), .in12({32{1'b0}}),
    .in13({32{1'b0}}), .in14({32{1'b0}}), .in15({32{1'b0}}), .out(Address), .sel(iCd));
  Multiplexer #(.select(4), .width(32), .enable("false")) multiplexer_2 (
    .in0({32{1'b0}}), .in1({32{1'b0}}), .in2({32{1'b0}}), .in3({32{1'b0}}), .in4(valA), .in5({32{1'b0}}),
    .in6({32{1'b0}}), .in7({32{1'b0}}), .in8(valP), .in9({32{1'b0}}), .in10(valA), .in11({32{1'b0}}),
    .in12({32{1'b0}}), .in13({32{1'b0}}), .in14({32{1'b0}}), .in15({32{1'b0}}), .out(Data), .sel(iCd));
  or or_1 (Write, do_not_click_here_double_click_module_in_circuit_equals_1_output, do_not_click_here_double_click_module_in_circuit_equals_2_output, do_not_click_here_double_click_module_in_circuit_equals_3_output);
endmodule

// PC Update
module Do_not_click_here__double_click_module_in_circuit_nextPC (
  input  [31:0] valP,
  input  bch,
  input  [31:0] valC,
  input  [31:0] valM,
  input  [3:0] iCd,
  output [31:0] nextPC
);

  wire [31:0] multiplexer_1_out;

  Multiplexer #(.width(32), .enable("false")) multiplexer_1 (
    .in0(valP), .in1(valC), .out(multiplexer_1_out), .sel(bch));
  Multiplexer #(.select(4), .width(32), .enable("false")) multiplexer_2 (
    .in0(valP), .in1(valP), .in2(valP), .in3(valP), .in4(valP), .in5(valP), .in6(valP),
    .in7(multiplexer_1_out), .in8(valC), .in9(valM), .in10(valP), .in11(valP), .in12(valP), .in13(valP),
    .in14(valP), .in15(valP), .out(nextPC), .sel(iCd));
endmodule

module Illegal_Memory_Access (
  input  Substep,
  input  [31:0] Address,
  output Output
);

  wire and_1_out, or_1_out;

  or or_1 (or_1_out, Address[0], Address[1]);
  and and_1 (and_1_out, Substep, or_1_out);
  or or_2 (Output, and_1_out, Address[24], Address[25], Address[26], Address[27], Address[28], Address[29], Address[30], Address[31]);
endmodule
