// Logisim project Y86_RAM.circ as structural Verilog: 1 circuit, main circuit main
module main (
  input  [31:0] Data_from_Memory_Storage,
  input  [7:0] Address,
  input  Write,
  input  Substep_num,
  output [31:0] Data__OUT
);

  wire and_1_out, Clock_out, not_1_out;

  Clock Clock (.out(Clock_out));
  assign Data__OUT = and_1_out ? Data_from_Memory_Storage : 32'bz;  // Controlled_Buffer controlled_buffer_1
  and and_1 (and_1_out, Write, Substep_num);
  not not_1 (not_1_out, and_1_out);
  RAM #(.dataWidth(32)) ram_1 (
    .addr(Address), .data(Data__OUT), .sel(1'b1), .clk(Clock_out), .ld(not_1_out), .clr(1'b0));
endmodule
