// Logisim project and_bug.circ as structural Verilog: 1 circuit, main circuit main
module main (
  output out_1
);

  wire and_1_out, clock_1_out, d_ff_1_qn, not_1_out;

  Clock clock_1 (.out(clock_1_out));
  not not_1 (not_1_out, clock_1_out);
  and and_1 (and_1_out, clock_1_out, not_1_out);
  D_Flip_Flop d_ff_1 (.clk(and_1_out), .D(d_ff_1_qn), .Q(out_1), .Qn(d_ff_1_qn));  // open: preset, en, reset
endmodule
