// Logisim project chains.circ as structural Verilog: 1 circuit, main circuit main
module main (
  input  A,
  input  B,
  input  C,
  input  D,
  output AND_chain,
  output OR_chain,
  output NAND_chain,
  output NOR_chain,
  output XOR_chain,
  output AND_tree,
  output OR_tree,
  output NAND_tree,
  output NOR_tree,
  output XOR_tree
);

  wire and_2_out, and_3_out, and_4_out, and_5_out, nand_1_out, nand_2_out, nand_3_out, nand_6_out, nor_1_out,
       nor_2_out, nor_4_out, nor_5_out, or_2_out, or_3_out, or_4_out, or_5_out, xor_2_out, xor_3_out,
       xor_4_out, xor_5_out;

  and and_1 (AND_chain, and_2_out, D);
  and and_2 (and_2_out, and_3_out, C);
  and and_3 (and_3_out, A, B);
  and and_4 (and_4_out, A, B);
  and and_5 (and_5_out, C, D);
  and and_6 (AND_tree, and_4_out, and_5_out);
  or or_1 (OR_chain, or_2_out, D);
  or or_2 (or_2_out, or_3_out, C);
  or or_3 (or_3_out, A, B);
  or or_4 (or_4_out, C, D);
  or or_5 (or_5_out, A, B);
  or or_6 (OR_tree, or_5_out, or_4_out);
  nand nand_1 (nand_1_out, nand_2_out, C);
  nand nand_2 (nand_2_out, A, B);
  nand nand_3 (nand_3_out, A, B);
  nand nand_4 (NAND_tree, nand_3_out, nand_6_out);
  nand nand_5 (NAND_chain, nand_1_out, D);
  nor nor_1 (nor_1_out, A, B);
  nand nand_6 (nand_6_out, C, D);
  nor nor_2 (nor_2_out, A, B);
  nor nor_3 (NOR_chain, nor_4_out, D);
  nor nor_4 (nor_4_out, nor_1_out, C);
  nor nor_5 (nor_5_out, C, D);
  nor nor_6 (NOR_tree, nor_2_out, nor_5_out);
  xor xor_1 (XOR_chain, xor_2_out, D);
  xor xor_2 (xor_2_out, xor_3_out, C);
  xor xor_3 (xor_3_out, A, B);
  xor xor_4 (xor_4_out, A, B);
  xor xor_5 (xor_5_out, C, D);
  xor xor_6 (XOR_tree, xor_4_out, xor_5_out);
endmodule
