// Logisim project conciseALU.circ as structural Verilog: 1 circuit, main circuit main
module main (
  input  [7:0] aluB,
  input  [7:0] aluA,
  input  [1:0] \function ,
  output valO,
  output [7:0] valE
);

  wire adder_1_cout, subtractor_1_bout;
  wire [7:0] adder_1_out, and_1_out, subtractor_1_out, xor_1_out;

  Adder adder_1 (.a(aluB), .b(aluA), .out(adder_1_out), .cout(adder_1_cout));  // open: cin
  Subtractor subtractor_1 (.a(aluB), .b(aluA), .out(subtractor_1_out), .bout(subtractor_1_bout));  // open: bin
  assign and_1_out = aluB & aluA;  // AND_Gate and_1, 8 bits wide
  assign xor_1_out = aluB ^ aluA;  // XOR_Gate xor_1, 8 bits wide
  Multiplexer #(.select(2), .width(8), .enable("false")) multiplexer_1 (
    .in0(adder_1_out), .in1(subtractor_1_out), .in2(and_1_out), .in3(xor_1_out), .out(valE), .sel(\function ));
  Multiplexer #(.select(2), .enable("false")) multiplexer_2 (
    .in0(adder_1_cout), .in1(subtractor_1_bout), .in2(1'b0), .in3(1'b0), .out(valO), .sel(\function ));
endmodule
