// Logisim project factorial_fixed.circ as structural Verilog: 1 circuit, main circuit Factorial Circuit
module Factorial_Circuit (
  output [15:0] n
);

  wire clock_1_out, d_ff_1_qn;
  wire [15:0] adder_1_out, multiplexer_1_out, n_q, register_1_q;

  Clock clock_1 (.out(clock_1_out));
  D_Flip_Flop d_ff_1 (.clk(clock_1_out), .D(1'b1), .Qn(d_ff_1_qn));  // open: Q, preset, en, reset
  Multiplexer #(.width(16), .enable("false")) multiplexer_1 (
    .in0(n), .in1(16'h1), .out(multiplexer_1_out), .sel(d_ff_1_qn));
  Register #(.width(16)) u_n (.D(adder_1_out), .Q(n_q), .clk(clock_1_out));  // open: en, clr
  Adder #(.width(16)) adder_1 (.a(n_q), .b(16'h1), .out(adder_1_out));  // open: cin, cout
  Register #(.width(16)) register_1 (.D(multiplexer_1_out), .Q(register_1_q), .clk(clock_1_out));  // open: en, clr
  Multiplier #(.width(16)) multiplier_1 (.a(n_q), .b(register_1_q), .out(n));  // open: cin, cout

  // Notes on the sheet:
  //   Factorial circuit
endmodule
