// Logisim project fibonacci.circ as structural Verilog: 1 circuit, main circuit Fibonacci Circuit
module Fibonacci_Circuit (
  output [15:0] fib_n
);

  wire clock_1_out, d_ff_1_qn;
  wire [15:0] fib_n_1_q, fib_n_2_q, multiplexer_1_out;

  Clock clock_1 (.out(clock_1_out));
  D_Flip_Flop d_ff_1 (.clk(clock_1_out), .D(1'b1), .Qn(d_ff_1_qn));  // open: Q, preset, en, reset
  Multiplexer #(.width(16), .enable("false")) multiplexer_1 (
    .in0(fib_n), .in1(16'h1), .out(multiplexer_1_out), .sel(d_ff_1_qn));
  Register #(.width(16)) fib_n_2 (.D(fib_n_1_q), .Q(fib_n_2_q), .clk(clock_1_out));  // open: en, clr
  Register #(.width(16)) fib_n_1 (.D(multiplexer_1_out), .Q(fib_n_1_q), .clk(clock_1_out));  // open: en, clr
  Adder #(.width(16)) adder_1 (.a(fib_n_2_q), .b(fib_n_1_q), .out(fib_n));  // open: cin, cout

  // Notes on the sheet:
  //   Fibonacci circuit
endmodule
