// Logisim project lab3q2a.circ as structural Verilog: 1 circuit, main circuit main
module main (
  input  a,
  input  b,
  input  c,
  input  d,
  input  a_2,
  input  b_2,
  input  c_2,
  input  d_2,
  output out_9,
  output out_10
);

  wire nand_1_out, nand_2_out, nand_3_out, nand_4_out, nand_5_out, nand_6_out, nand_8_out, nand_9_out,
       nand_10_out, nand_11_out;

  nand nand_1 (nand_1_out, a, b);
  nand nand_2 (nand_2_out, c, d);
  nand nand_3 (nand_3_out, a_2, b_2);
  nand nand_4 (nand_4_out, c_2, d_2);
  nand nand_5 (nand_5_out, nand_3_out, nand_3_out);
  nand nand_6 (nand_6_out, nand_4_out, nand_4_out);
  nand nand_7 (out_9, nand_1_out, nand_2_out);
  nand nand_8 (nand_8_out, nand_5_out, nand_5_out);
  nand nand_9 (nand_9_out, nand_6_out, nand_6_out);
  nand nand_10 (nand_10_out, nand_8_out, nand_9_out);
  nand nand_11 (nand_11_out, nand_10_out, nand_10_out);
  nand nand_12 (out_10, nand_11_out, nand_11_out);
endmodule
