// Logisim project lab3challenge.circ as structural Verilog: 1 circuit, main circuit main
module main (
  input  a,
  input  in_2,
  input  b,
  input  c,
  input  d,
  input  in_6,
  output out_7,
  output out_8,
  output out_9,
  output out_10,
  output out_11,
  output out_12
);

  wire undriven;
  wire [2:0] priority_encoder_1_out;

  Priority_Encoder priority_encoder_1 (
    .in0(a), .in1(b), .in2(c), .in3(d), .out(priority_encoder_1_out), .en_in(undriven), .gs(out_12),
    .en_out(out_9));  // open: in4, in5, in6, in7
  Decoder #(.select(3), .disabled(0)) decoder_1 (
    .out0(out_7), .out1(out_8), .out2(out_10), .out3(out_11), .sel(priority_encoder_1_out), .en(in_2));  // open: out4, out5, out6, out7
endmodule
