// Logisim project lab4-1to2demux.circ as structural Verilog: 1 circuit, main circuit main
module main (
  input  s,
  input  y,
  output x0,
  output x1
);

  wire not_1_out;

  not not_1 (not_1_out, s);
  and and_1 (x0, not_1_out, y);
  and and_2 (x1, s, y);
endmodule
