// Logisim project lab4-1to4demux.circ as structural Verilog: 1 circuit, main circuit main
module main (
  input  y,
  input  select1,
  input  select0,
  output x0,
  output x1,
  output x2,
  output x3
);

  wire demultiplexer_1_out0, demultiplexer_1_out1;

  Demultiplexer demultiplexer_1 (
    .out0(demultiplexer_1_out0), .out1(demultiplexer_1_out1), .in(y), .sel(select1));  // open: en
  Demultiplexer demultiplexer_2 (.out0(x0), .out1(x1), .in(demultiplexer_1_out0), .sel(select0));  // open: en
  Demultiplexer demultiplexer_3 (.out0(x2), .out1(x3), .in(demultiplexer_1_out1), .sel(select0));  // open: en
endmodule
