// Logisim project lab4q3.circ as structural Verilog: 1 circuit, main circuit main
module main (
  input  a,
  input  b,
  input  s,
  output out_4
);

  wire and_1_out, xor_1_out;

  and and_1 (and_1_out, a, b);
  xor xor_1 (xor_1_out, a, b);
  Multiplexer multiplexer_1 (.in0(and_1_out), .in1(xor_1_out), .out(out_4), .sel(s));  // open: en
endmodule
