// Logisim project lab5flipflop.circ as structural Verilog: 1 circuit, main circuit main
module main (
  input  d,
  input  en,
  output out_3
);

  Multiplexer multiplexer_1 (.in0(out_3), .in1(d), .out(out_3), .sel(en));  // open: en
endmodule
