// Logisim project lab6-prelab.circ as structural Verilog: 1 circuit, main circuit main
module main (
  input  [15:0] in_1,
  input  in_2,
  output [15:0] out_3
);

  wire clock_1_out;
  wire [15:0] adder_1_out;

  Clock clock_1 (.out(clock_1_out));
  Adder #(.width(16)) adder_1 (.a(out_3), .b(in_1), .out(adder_1_out));  // open: cin, cout
  Register #(.width(16)) register_1 (.D(adder_1_out), .Q(out_3), .clk(clock_1_out), .clr(in_2));  // open: en

  // Notes on the sheet:
  //   Sequential circuit that simulates counting by 2
endmodule
