// Logisim project piso_sipo.circ as structural Verilog: 1 circuit, main circuit main
module main (
  input  A,
  input  B,
  input  C,
  input  D,
  output W,
  output X,
  output Y,
  output Z,
  output [1:0] out_9
);

  wire clock_1_out, d_ff_1_q, d_ff_2_q, d_ff_3_q, d_ff_4_q, d_ff_5_qn, d_ff_6_qn, multiplexer_1_out,
       not_1_out;

  Clock clock_1 (.out(clock_1_out));
  D_Flip_Flop d_ff_1 (.clk(clock_1_out), .D(A), .Q(d_ff_1_q));  // open: Qn, preset, en, reset
  D_Flip_Flop d_ff_2 (.clk(clock_1_out), .D(B), .Q(d_ff_2_q));  // open: Qn, preset, en, reset
  D_Flip_Flop d_ff_3 (.clk(clock_1_out), .D(C), .Q(d_ff_3_q));  // open: Qn, preset, en, reset
  D_Flip_Flop d_ff_4 (.clk(clock_1_out), .D(D), .Q(d_ff_4_q));  // open: Qn, preset, en, reset
  not not_1 (not_1_out, clock_1_out);
  Multiplexer #(.select(2), .enable("false")) multiplexer_1 (
    .in0(d_ff_1_q), .in1(d_ff_2_q), .in2(d_ff_3_q), .in3(d_ff_4_q), .out(multiplexer_1_out), .sel(out_9));
  D_Flip_Flop d_ff_5 (.clk(clock_1_out), .D(d_ff_5_qn), .Q(out_9[1]), .Qn(d_ff_5_qn));  // open: preset, en, reset
  D_Flip_Flop d_ff_6 (.clk(out_9[1]), .D(d_ff_6_qn), .Q(out_9[0]), .Qn(d_ff_6_qn));  // open: preset, en, reset
  D_Flip_Flop d_ff_7 (.clk(not_1_out), .D(multiplexer_1_out), .Q(W));  // open: Qn, preset, en, reset
  D_Flip_Flop d_ff_8 (.clk(not_1_out), .D(W), .Q(X));  // open: Qn, preset, en, reset
  D_Flip_Flop d_ff_9 (.clk(not_1_out), .D(X), .Q(Y));  // open: Qn, preset, en, reset
  D_Flip_Flop d_ff_10 (.clk(not_1_out), .D(Y), .Q(Z));  // open: Qn, preset, en, reset
endmodule
