// Logisim project priority.circ as structural Verilog: 2 circuits, main circuit main
module main (
  input  in_1,
  input  in_2,
  input  in_3,
  input  in_4,
  input  in_5,
  input  in_6,
  output out_7,
  output out_8,
  output out_9,
  output out_10,
  output out_11,
  output out_12,
  output out_13
);

  wire p_1_y, p_2_y, p_3_y, p_4_y, p_5_y;

  P p_1 (.a(1'b0), .y(p_1_y), .x(out_7), .b(in_1));
  P p_2 (.a(p_1_y), .y(p_2_y), .x(out_8), .b(in_2));
  P p_3 (.a(p_2_y), .y(p_3_y), .x(out_9), .b(in_3));
  P p_4 (.a(p_3_y), .y(p_4_y), .x(out_10), .b(in_4));
  P p_5 (.a(p_4_y), .y(p_5_y), .x(out_11), .b(in_5));
  P p_6 (.a(p_5_y), .y(out_13), .x(out_12), .b(in_6));
endmodule

module P (
  input  a,
  input  b,
  output x,
  output y
);

  wire not_1_out;

  not not_1 (not_1_out, a);
  and and_1 (x, not_1_out, b);
  or or_1 (y, a, b);
endmodule
